# Fritzing sketch esquematico_v1 (saved by Fritzing 0.9.10b)
breadboards: 1

parts:
  S1 = Tactile Switch Buttons - 12mm Square [package=tactile-pth-12mm]
  Componente1 = Arduino Pro Micro (Clone)
  S2 = Tactile Switch Buttons - 12mm Square [package=tactile-pth-12mm]
  S3 = Tactile Switch Buttons - 12mm Square [package=tactile-pth-12mm]
  S4 = Tactile Switch Buttons - 12mm Square [package=tactile-pth-12mm]
  S5 = Tactile Switch Buttons - 12mm Square [package=tactile-pth-12mm]
  S6 = Tactile Switch Buttons - 12mm Square [package=tactile-pth-12mm]
  S7 = Tactile Switch Buttons - 12mm Square [package=tactile-pth-12mm]
  S8 = Tactile Switch Buttons - 12mm Square [package=tactile-pth-12mm]
  R2 = Resistor [tolerance=±5% power=0.25 resistance=470 package=THT]
  R3 = Resistor [tolerance=±5% power=0.25 resistance=470 package=THT]
  LED1 = LED - 5mm [color="Red (633nm)" current=0.030 package="5 mm [THT]"]
  LED2 = LED - 5mm [color="Blue (430nm)" current=0.030 package="5 mm [THT]"]
  R4 = Resistor [tolerance=±5% power=0.25 resistance=470 package=THT]
  LED3 = LED - 5mm [color="Yellow (595nm)" current=0.030 package="5 mm [THT]"]
  R5 = Rotary Potentiometer (Small) [maximum_resistance=100kΩ knob_status=50% power=0.5W package=THT]
  R6 = Rotary Potentiometer (Small) [maximum_resistance=100kΩ knob_status=50% power=0.5W package=THT]
  R7 = Rotary Potentiometer (Small) [maximum_resistance=100kΩ knob_status=50% power=0.5W package=THT]
  S9 = Tactile Switch Buttons - 12mm Square [package=tactile-pth-12mm]

nets:
  N1: S1.1, S1.3, Componente1.GND, S2.1, S2.3, S3.1, S3.3, S4.1, S4.3, S5.1, S5.3, S6.1, S6.3, S7.1, S7.3, S8.1, S8.3, R2.Pin_1, R3.Pin_1, R4.Pin_1, R5.leg1, R6.leg1, R7.leg1, S9.1, S9.3
  N2: S1.2, S1.4, Componente1.D2
  N3: Componente1.D3, S2.2, S2.4
  N4: Componente1.D4, S3.2, S3.4
  N5: Componente1.D5, S4.2, S4.4
  N6: Componente1.D6, S5.2
  N7: Componente1.D7, S6.2
  N8: Componente1.D8, LED2.anode
  N9: Componente1.D9, LED1.anode
  N10: Componente1.D10, S9.2
  N11: Componente1.D16, LED3.anode
  N12: Componente1.D14, S8.2
  N13: Componente1.D15, S7.2
  N14: Componente1.A0, R7.wiper
  N15: Componente1.A1, R6.wiper
  N16: Componente1.A2, R5.wiper
  N17: Componente1.VCC, R5.leg2, R6.leg2, R7.leg2
  N18: R2.Pin_0, LED2.cathode
  N19: R3.Pin_0, LED1.cathode
  N20: R4.Pin_0, LED3.cathode

custom parts:
  Tactile Switch Buttons - 12mm Square: Medium-sized clicky momentary switches are standard input "buttons" on electronic projects. These work best in a PCB but can be used on a solderless breadboard as shown in this tutorial. The pins are normally open (disconnected) and when the button is pressed they are momentarily closed. They come in a pack of 10, they're pretty handy so you'll want to keep them around. You can find an EAGLE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
