# Fritzing sketch testes (saved by Fritzing 0.9.10b)
circuit board: 12.0194cm x 7.23128cm
circuit board: 11.9668cm x 5.66971cm

parts:
  Componente1 = Arduino Pro Micro (Clone)
  Componente2 = Analog Digital MUX Breakout
  S1 = Tactile Switch Buttons - 12mm Square [package=tactile-pth-12mm]
  S2 = Tactile Switch Buttons - 12mm Square [package=tactile-pth-12mm]
  S3 = Tactile Switch Buttons - 12mm Square [package=tactile-pth-12mm]
  S4 = Tactile Switch Buttons - 12mm Square [package=tactile-pth-12mm]
  S5 = Tactile Switch Buttons - 12mm Square [package=tactile-pth-12mm]
  S6 = Tactile Switch Buttons - 12mm Square [package=tactile-pth-12mm]
  S7 = Tactile Switch Buttons - 12mm Square [package=tactile-pth-12mm]
  S8 = Tactile Switch Buttons - 12mm Square [package=tactile-pth-12mm]
  S9 = Tactile Switch Buttons - 12mm Square [package=tactile-pth-12mm]
  S10 = Tactile Switch Buttons - 12mm Square [package=tactile-pth-12mm]
  S11 = Tactile Switch Buttons - 12mm Square [package=tactile-pth-12mm]
  S12 = Tactile Switch Buttons - 12mm Square [package=tactile-pth-12mm]
  S13 = Tactile Switch Buttons - 12mm Square [package=tactile-pth-12mm]
  S14 = Tactile Switch Buttons - 12mm Square [package=tactile-pth-12mm]
  S15 = Tactile Switch Buttons - 12mm Square [package=tactile-pth-12mm]
  S16 = Tactile Switch Buttons - 12mm Square [package=tactile-pth-12mm]
  S17 = Tactile Switch Buttons - 12mm Square [package=tactile-pth-12mm]
  S18 = Tactile Switch Buttons - 12mm Square [package=tactile-pth-12mm]
  S19 = Tactile Switch Buttons - 12mm Square [package=tactile-pth-12mm]
  S20 = Tactile Switch Buttons - 12mm Square [package=tactile-pth-12mm]
  R1 = Slide Potentiometer [maximum_resistance=10kΩ knob_status=50% power=0.5W]
  R2 = Slide Potentiometer [maximum_resistance=10kΩ knob_status=50% power=0.5W]
  R3 = Slide Potentiometer [maximum_resistance=10kΩ knob_status=50% power=0.5W]
  R4 = Slide Potentiometer [maximum_resistance=10kΩ knob_status=50% power=0.5W]

nets:
  GND: Componente1.GND, Componente2.GND, Componente2.EN, S1.2, S1.4, S2.2, S2.4, S3.2, S3.4, S4.2, S4.4, S5.2, S5.4, S6.2, S6.4, S7.2, S7.4, S8.2, S8.4, S9.2, S9.4, S10.2, S10.4, S11.2, S11.4, S12.2, S12.4, S13.2, S13.4, S14.2, S14.4, S15.2, S16.2, S16.4, R1.leg1, R2.leg1, R3.leg1, R4.leg1
  N1: Componente1.D4, Componente2.SIG
  N2: Componente1.D6, Componente2.S3
  N3: Componente1.D7, Componente2.S2
  N4: Componente1.D8, Componente2.S1
  N5: Componente1.D9, Componente2.S0
  N6: Componente1.D10, S19.1, S19.3
  N7: Componente1.D16, S17.1, S17.3
  N8: Componente1.D14, S20.1, S20.3
  N9: Componente1.D15, S18.1, S18.3
  N10: Componente1.A0, R1.wiper
  N11: Componente1.A1, R2.wiper
  N12: Componente1.A2, R3.wiper
  N13: Componente1.A3, R4.wiper
  VCC: Componente1.VCC, Componente2.VCC, R1.leg2, R2.leg2, R3.leg2, R4.leg2
  N14: Componente2.C0, S1.1, S1.3
  N15: Componente2.C1, S2.1, S2.3
  N16: Componente2.C2, S3.1, S3.3
  N17: Componente2.C3, S4.1, S4.3
  N18: Componente2.C4, S8.1, S8.3
  N19: Componente2.C5, S6.1, S6.3
  N20: Componente2.C6, S5.1, S5.3
  N21: Componente2.C7, S7.1, S7.3
  N22: Componente2.C8, S12.1, S12.3
  N23: Componente2.C9, S10.1, S10.3
  N24: Componente2.C10, S9.1, S9.3
  N25: Componente2.C11, S11.1, S11.3
  N26: Componente2.C12, S16.1, S16.3
  N27: Componente2.C13, S14.1, S14.3
  N28: Componente2.C14, S13.1, S13.3
  N29: Componente2.C15, S15.1, S15.3
  N30: S17.2, S17.4, S18.2, S18.4, S19.2, S19.4, S20.2, S20.4

custom parts:
  Tactile Switch Buttons - 12mm Square: Medium-sized clicky momentary switches are standard input "buttons" on electronic projects. These work best in a PCB but can be used on a solderless breadboard as shown in this tutorial. The pins are normally open (disconnected) and when the button is pressed they are momentarily closed. They come in a pack of 10, they're pretty handy so you'll want to keep them around. You can find an EAGLE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
